# Fritzing sketch node-demo-arduino (saved by Fritzing 0.8.3b)
breadboards: 1

parts:
  Composants1 = Arduino Uno (Rev3)
  R1 = Resistor [tolerance=±5% resistance=150 package=THT]
  R2 = Resistor [tolerance=±5% resistance=150 package=THT]
  R3 = Resistor [tolerance=±5% resistance=150 package=THT]
  LED1 = LED - 5mm [color="Red (633nm)" package="5 mm [THT]"]
  LED2 = LED - 5mm [color="Yellow (595nm)" package="5 mm [THT]"]
  LED3 = LED - 5mm [color="Green (565nm)" package="5 mm [THT]"]
  LCD1 = LCD screen
  R4 = Rotary Potentiometer (Small)

nets:
  N1: Composants1.ICSP_MISO, Composants1.D12/MISO, R1.Pin_0
  N2: Composants1.ICSP_SCK, Composants1.D13/SCK, R3.Pin_0
  N3: Composants1.ICSP_MOSI, Composants1.D11_PWM/MOSI, R2.Pin_0
  N4: Composants1.D8, LCD1.DB5
  N5: Composants1.D9_PWM, LCD1.DB6
  N6: Composants1.D10_PWM/SS, LCD1.DB7
  N7: Composants1.D5_PWM, LCD1.RS
  N8: Composants1.D6_PWM, LCD1.E
  N9: Composants1.D7, LCD1.DB4
  5V: Composants1.5V, LCD1.VDD, LCD1.LED+, R4.leg1
  N10: R1.Pin_1, LED2.anode
  N11: R2.Pin_1, LED3.anode
  N12: R3.Pin_1, LED1.anode
  N13: LED1.cathode, LED2.cathode, LED3.cathode, LCD1.VSS, LCD1.R/W, LCD1.LED-, R4.leg2
  N14: LCD1.V0, R4.wiper
